// Logisim project 1931741642 Asfaria Islam Chowdhury.circ as structural Verilog: 2 circuits, main circuit main
module main (
  input  [2:0] A,
  input  [2:0] B,
  input  [1:0] S,
  output [2:0] F
);

  wire and_1_out, and_2_out, and_3_out, nand_1_out, nand_2_out, nand_3_out, nor_1_out, nor_2_out, nor_3_out,
       xor_1_out, xor_2_out, xor_3_out;

  nand nand_1 (nand_1_out, A[0], B[0]);
  nor nor_1 (nor_1_out, A[0], B[0]);
  and and_1 (and_1_out, A[0], B[0]);
  xor xor_1 (xor_1_out, A[0], B[0]);
  nand nand_2 (nand_2_out, A[1], B[1]);
  nor nor_2 (nor_2_out, A[1], B[1]);
  and and_2 (and_2_out, A[1], B[1]);
  xor xor_2 (xor_2_out, A[1], B[1]);
  nand nand_3 (nand_3_out, A[2], B[2]);
  nor nor_3 (nor_3_out, A[2], B[2]);
  and and_3 (and_3_out, A[2], B[2]);
  xor xor_3 (xor_3_out, A[2], B[2]);
  Multiplexer #(.select(2)) multiplexer_1 (
    .in0(nand_1_out), .in1(nor_1_out), .in2(and_1_out), .in3(xor_1_out), .out(F[0]), .sel(S));  // open: en
  Multiplexer #(.select(2)) multiplexer_2 (
    .in0(nand_2_out), .in1(nor_2_out), .in2(and_2_out), .in3(xor_2_out), .out(F[1]), .sel(S));  // open: en
  Multiplexer #(.select(2)) multiplexer_3 (
    .in0(nand_3_out), .in1(nor_3_out), .in2(and_3_out), .in3(xor_3_out), .out(F[2]), .sel(S));  // open: en
endmodule

module USR (
  input  S,
  input  Shift_Left,
  input  Shift_Right
);

  wire clock_1_out, d_ff_1_q, d_ff_2_q, d_ff_3_q, d_ff_4_q, d_ff_5_q, multiplexer_1_out, multiplexer_2_out,
       multiplexer_3_out, multiplexer_4_out, multiplexer_5_out;

  Multiplexer multiplexer_1 (.in0(Shift_Left), .in1(d_ff_2_q), .out(multiplexer_1_out), .sel(S));  // open: en
  Multiplexer multiplexer_2 (.in0(d_ff_1_q), .in1(d_ff_3_q), .out(multiplexer_2_out), .sel(S));  // open: en
  Multiplexer multiplexer_3 (.in0(d_ff_2_q), .in1(d_ff_4_q), .out(multiplexer_3_out), .sel(S));  // open: en
  Multiplexer multiplexer_4 (.in0(d_ff_3_q), .in1(d_ff_5_q), .out(multiplexer_4_out), .sel(S));  // open: en
  Multiplexer multiplexer_5 (.in0(d_ff_4_q), .in1(Shift_Right), .out(multiplexer_5_out), .sel(S));  // open: en
  D_Flip_Flop d_ff_1 (.clk(clock_1_out), .D(multiplexer_1_out), .Q(d_ff_1_q));  // open: Qn, preset, en, reset
  D_Flip_Flop d_ff_2 (.clk(clock_1_out), .D(multiplexer_2_out), .Q(d_ff_2_q));  // open: Qn, preset, en, reset
  D_Flip_Flop d_ff_3 (.clk(clock_1_out), .D(multiplexer_3_out), .Q(d_ff_3_q));  // open: Qn, preset, en, reset
  D_Flip_Flop d_ff_4 (.clk(clock_1_out), .D(multiplexer_4_out), .Q(d_ff_4_q));  // open: Qn, preset, en, reset
  D_Flip_Flop d_ff_5 (.clk(clock_1_out), .D(multiplexer_5_out), .Q(d_ff_5_q));  // open: Qn, preset, en, reset
  Clock clock_1 (.out(clock_1_out));
endmodule
