// Logisim project 12-bit Datapath-1.circ as structural Verilog: 3 circuits, main circuit main
module main (
  output [11:0] Result,
  output [11:0] R2,
  output [11:0] R1,
  output [11:0] out_4
);

  wire CLK_out;
  wire [2:0] rom_1_data, rom_1_data_2, rom_1_data_3;
  wire [11:0] adder_1_out, PC_q;
  wire [11:9] rom_1_data_4;

  Adder #(.width(12)) adder_1 (.a(12'h1), .b(PC_q), .out(adder_1_out));  // open: cin, cout
  Register #(.width(12)) PC (.D(adder_1_out), .Q(PC_q), .clk(CLK_out));  // open: en, clr
  Button CLK (.out(CLK_out));
  Register_File register_file_1 (
    .in_1(rom_1_data_3), .in_2(Result), .in_3(rom_1_data_2), .in_4(rom_1_data), .in_5(CLK_out), .out_6(R1),
    .out_7(R2));
  ROM #(.addrWidth(12), .dataWidth(12)) rom_1 (
    .addr(PC_q), .data({rom_1_data_4, rom_1_data_3, rom_1_data_2, rom_1_data}));  // open: sel
  ALU alu_1 (.in_1(R1), .in_2(R2), .in_3(rom_1_data_4), .out_4(Result));
  RAM #(.addrWidth(12), .dataWidth(12)) ram_1 (.addr(Result), .data(out_4), .clk(CLK_out));  // open: sel, ld, clr

  // Notes on the sheet:
  //   contents of rom_1 (hex, n*v repeats v):
  //   641 2a3 84d b77 f6 45c
  //   rd
  //   rt
  //   rs
  //   opcode
endmodule

module Register_File (
  input  [2:0] in_1,
  input  [11:0] in_2,
  input  [2:0] in_3,
  input  [2:0] in_4,
  input  in_5,
  output [11:0] out_6,
  output [11:0] out_7
);

  wire decoder_1_out0, decoder_1_out1, decoder_1_out2, decoder_1_out3, decoder_1_out4, decoder_1_out5,
       decoder_1_out6, decoder_1_out7;
  wire [11:0] register_1_q, register_2_q, register_3_q, register_4_q, register_5_q, register_6_q,
       register_7_q, register_8_q;

  Decoder #(.select(3), .enable("false")) decoder_1 (
    .out0(decoder_1_out0), .out1(decoder_1_out1), .out2(decoder_1_out2), .out3(decoder_1_out3),
    .out4(decoder_1_out4), .out5(decoder_1_out5), .out6(decoder_1_out6), .out7(decoder_1_out7), .sel(in_4));
  Register #(.width(12)) register_1 (.D(in_2), .en(decoder_1_out0), .Q(register_1_q), .clk(in_5));  // open: clr
  Register #(.width(12)) register_2 (.D(in_2), .en(decoder_1_out1), .Q(register_2_q), .clk(in_5));  // open: clr
  Register #(.width(12)) register_3 (.D(in_2), .en(decoder_1_out2), .Q(register_3_q), .clk(in_5));  // open: clr
  Register #(.width(12)) register_4 (.D(in_2), .en(decoder_1_out3), .Q(register_4_q), .clk(in_5));  // open: clr
  Register #(.width(12)) register_5 (.D(in_2), .en(decoder_1_out4), .Q(register_5_q), .clk(in_5));  // open: clr
  Register #(.width(12)) register_6 (.D(in_2), .en(decoder_1_out5), .Q(register_6_q), .clk(in_5));  // open: clr
  Register #(.width(12)) register_7 (.D(in_2), .en(decoder_1_out6), .Q(register_7_q), .clk(in_5));  // open: clr
  Register #(.width(12)) register_8 (.D(in_2), .en(decoder_1_out7), .Q(register_8_q), .clk(in_5));  // open: clr
  Multiplexer #(.select(3), .width(12), .enable("false")) multiplexer_1 (
    .in0(register_1_q), .in1(register_2_q), .in2(register_3_q), .in3(register_4_q), .in4(register_5_q),
    .in5(register_6_q), .in6(register_7_q), .in7(register_8_q), .out(out_6), .sel(in_1));
  Multiplexer #(.select(3), .width(12), .enable("false")) multiplexer_2 (
    .in0(register_1_q), .in1(register_2_q), .in2(register_3_q), .in3(register_4_q), .in4(register_5_q),
    .in5(register_6_q), .in6(register_7_q), .in7(register_8_q), .out(out_7), .sel(in_3));
endmodule

module ALU (
  input  [11:0] in_1,
  input  [11:0] in_2,
  input  [2:0] in_3,
  output [11:0] out_4
);

  wire adder_1_cout, adder_2_cout, comparator_1_lt;
  wire [3:0] bit_extender_1_out;
  wire [11:0] adder_1_out, adder_2_out, and_1_out, bit_extender_2_out, not_1_out, or_1_out, shifter_1_out;

  assign not_1_out = ~in_2;  // NOT_Gate not_1, 12 bits wide
  Bit_Extender #(.in_width(12), .out_width(4)) bit_extender_1 (.in(in_2), .out(bit_extender_1_out));
  Comparator #(.width(12)) comparator_1 (.a(in_1), .b(in_2), .lt(comparator_1_lt));  // open: gt, eq
  assign and_1_out = in_1 & in_2;  // AND_Gate and_1, 12 bits wide
  assign or_1_out = in_1 | in_2;  // OR_Gate or_1, 12 bits wide
  Adder #(.width(12)) adder_1 (.a(in_1), .b(in_2), .out(adder_1_out), .cin(1'b0), .cout(adder_1_cout));
  Adder #(.width(12)) adder_2 (.a(in_1), .b(not_1_out), .out(adder_2_out), .cin(1'b1), .cout(adder_2_cout));
  Shifter #(.width(12)) shifter_1 (.in(in_1), .\dist (bit_extender_1_out), .out(shifter_1_out));
  assign bit_extender_2_out = {{11{1'b0}}, comparator_1_lt};  // Bit_Extender bit_extender_2
  Multiplexer #(.select(3), .width(12), .enable("false")) multiplexer_1 (
    .in0(and_1_out), .in1(or_1_out), .in2(adder_1_out), .in3(adder_2_out), .in4(shifter_1_out),
    .in5(bit_extender_2_out), .out(out_4), .sel(in_3));  // open: in6, in7
endmodule
