// Logisim project Lab2.circ as structural Verilog: 1 circuit, main circuit main
module main (
  input  Cin,
  input  S1,
  input  S0,
  input  A1,
  input  A0,
  input  B1,
  input  B0,
  output D0,
  output D1,
  output out_10
);

  wire adder_1_cout, multiplexer_1_out, multiplexer_2_out, not_1_out, not_2_out;

  not not_1 (not_1_out, B1);
  not not_2 (not_2_out, B0);
  Multiplexer #(.select(2), .enable("false")) multiplexer_1 (
    .in0(B0), .in1(not_2_out), .in2(1'b0), .in3(1'b1), .out(multiplexer_1_out), .sel({S1, S0}));
  Multiplexer #(.select(2), .enable("false")) multiplexer_2 (
    .in0(B1), .in1(not_1_out), .in2(1'b0), .in3(1'b1), .out(multiplexer_2_out), .sel({S1, S0}));
  Adder #(.width(1)) adder_1 (.a(A0), .b(multiplexer_1_out), .out(D0), .cin(Cin), .cout(adder_1_cout));
  Adder #(.width(1)) adder_2 (.a(A1), .b(multiplexer_2_out), .out(D1), .cin(adder_1_cout), .cout(out_10));

  // Notes on the sheet:
  //   MUX 0
  //   MUX 1
  //   Y0
  //   Y1
  //   Cout
endmodule
