// Logisim project Lab3.circ as structural Verilog: 1 circuit, main circuit main
module main (
  input  shift_right,
  input  I4,
  input  I3,
  input  I2,
  input  _11,
  input  S1,
  input  S0,
  input  CLR,
  input  shift_left,
  output A4,
  output A3,
  output A2,
  output A1
);

  wire CLK_out, multiplexer_1_out, multiplexer_2_out, multiplexer_3_out, multiplexer_4_out;

  Multiplexer #(.select(2)) multiplexer_1 (
    .in0(A4), .in1(shift_right), .in2(A3), .in3(I4), .out(multiplexer_1_out), .sel({S1, S0}));  // open: en
  Multiplexer #(.select(2)) multiplexer_2 (
    .in0(A3), .in1(A4), .in2(A2), .in3(I3), .out(multiplexer_2_out), .sel({S1, S0}));  // open: en
  Multiplexer #(.select(2)) multiplexer_3 (
    .in0(A2), .in1(A3), .in2(A1), .in3(I2), .out(multiplexer_3_out), .sel({S1, S0}));  // open: en
  Multiplexer #(.select(2)) multiplexer_4 (
    .in0(A1), .in1(A2), .in2(shift_left), .in3(_11), .out(multiplexer_4_out), .sel({S1, S0}));  // open: en
  D_Flip_Flop F4 (.clk(CLK_out), .D(multiplexer_1_out), .Q(A4), .reset(CLR));  // open: Qn, preset, en
  D_Flip_Flop F3 (.clk(CLK_out), .D(multiplexer_2_out), .Q(A3), .reset(CLR));  // open: Qn, preset, en
  D_Flip_Flop F2 (.clk(CLK_out), .D(multiplexer_3_out), .Q(A2), .reset(CLR));  // open: Qn, preset, en
  D_Flip_Flop F1 (.clk(CLK_out), .D(multiplexer_4_out), .Q(A1), .reset(CLR));  // open: Qn, preset, en
  Clock CLK (.out(CLK_out));
endmodule
