// Logisim project Lab6.circ as structural Verilog: 6 circuits, main circuit main
module main (
  input  [15:0] Write_Data,
  input  CLK,
  input  [3:0] Read_Register_1,
  input  [3:0] Read_Register_2,
  input  WriteEn,
  input  [3:0] Write_Register,
  output [15:0] Read_Data_1,
  output [15:0] Read_Data_1_2
);

  wire and_1_out, and_2_out, and_3_out, and_4_out, and_5_out, and_6_out, and_7_out, and_8_out, and_9_out,
       and_10_out, and_11_out, and_12_out, and_13_out, and_14_out, and_15_out, and_16_out, decoder_1_out0,
       decoder_1_out1, decoder_1_out2, decoder_1_out3, decoder_1_out4, decoder_1_out5, decoder_1_out6,
       decoder_1_out7, decoder_1_out8, decoder_1_out9, decoder_1_out10, decoder_1_out11, decoder_1_out12,
       decoder_1_out13, decoder_1_out14, decoder_1_out15;
  wire [15:0] R0_q, R1_q, R2_q, R3_q, R4_q, R5_q, R6_q, R7_q, R8_q, R9_q, R10_q, R11_q, R12_q, R13_q, R14_q,
       R15_q;

  Decoder #(.select(4)) decoder_1 (
    .out0(decoder_1_out0), .out1(decoder_1_out1), .out2(decoder_1_out2), .out3(decoder_1_out3),
    .out4(decoder_1_out4), .out5(decoder_1_out5), .out6(decoder_1_out6), .out7(decoder_1_out7),
    .out8(decoder_1_out8), .out9(decoder_1_out9), .out10(decoder_1_out10), .out11(decoder_1_out11),
    .out12(decoder_1_out12), .out13(decoder_1_out13), .out14(decoder_1_out14), .out15(decoder_1_out15),
    .sel(Write_Register));  // open: en
  and and_1 (and_1_out, WriteEn, decoder_1_out0);
  and and_2 (and_2_out, WriteEn, decoder_1_out1);
  and and_3 (and_3_out, WriteEn, decoder_1_out2);
  and and_4 (and_4_out, WriteEn, decoder_1_out3);
  and and_5 (and_5_out, WriteEn, decoder_1_out4);
  and and_6 (and_6_out, WriteEn, decoder_1_out5);
  and and_7 (and_7_out, WriteEn, decoder_1_out6);
  and and_8 (and_8_out, WriteEn, decoder_1_out7);
  Register #(.width(16)) R0 (.D(Write_Data), .en(and_1_out), .Q(R0_q), .clk(CLK));  // open: clr
  Register #(.width(16)) R1 (.D(Write_Data), .en(and_2_out), .Q(R1_q), .clk(CLK));  // open: clr
  Register #(.width(16)) R2 (.D(Write_Data), .en(and_3_out), .Q(R2_q), .clk(CLK));  // open: clr
  Register #(.width(16)) R3 (.D(Write_Data), .en(and_4_out), .Q(R3_q), .clk(CLK));  // open: clr
  Register #(.width(16)) R4 (.D(Write_Data), .en(and_5_out), .Q(R4_q), .clk(CLK));  // open: clr
  Register #(.width(16)) R5 (.D(Write_Data), .en(and_6_out), .Q(R5_q), .clk(CLK));  // open: clr
  Register #(.width(16)) R6 (.D(Write_Data), .en(and_7_out), .Q(R6_q), .clk(CLK));  // open: clr
  Register #(.width(16)) R7 (.D(Write_Data), .en(and_8_out), .Q(R7_q), .clk(CLK));  // open: clr
  and and_9 (and_9_out, WriteEn, decoder_1_out15);
  and and_10 (and_10_out, WriteEn, decoder_1_out14);
  and and_11 (and_11_out, WriteEn, decoder_1_out13);
  and and_12 (and_12_out, WriteEn, decoder_1_out12);
  and and_13 (and_13_out, WriteEn, decoder_1_out11);
  and and_14 (and_14_out, WriteEn, decoder_1_out10);
  and and_15 (and_15_out, WriteEn, decoder_1_out9);
  and and_16 (and_16_out, WriteEn, decoder_1_out8);
  Register #(.width(16)) R15 (.D(Write_Data), .en(and_9_out), .Q(R15_q), .clk(CLK));  // open: clr
  Register #(.width(16)) R14 (.D(Write_Data), .en(and_10_out), .Q(R14_q), .clk(CLK));  // open: clr
  Register #(.width(16)) R13 (.D(Write_Data), .en(and_11_out), .Q(R13_q), .clk(CLK));  // open: clr
  Register #(.width(16)) R12 (.D(Write_Data), .en(and_12_out), .Q(R12_q), .clk(CLK));  // open: clr
  Register #(.width(16)) R11 (.D(Write_Data), .en(and_13_out), .Q(R11_q), .clk(CLK));  // open: clr
  Register #(.width(16)) R10 (.D(Write_Data), .en(and_14_out), .Q(R10_q), .clk(CLK));  // open: clr
  Register #(.width(16)) R9 (.D(Write_Data), .en(and_15_out), .Q(R9_q), .clk(CLK));  // open: clr
  Register #(.width(16)) R8 (.D(Write_Data), .en(and_16_out), .Q(R8_q), .clk(CLK));  // open: clr
  Multiplexer #(.select(4), .width(16)) multiplexer_1 (
    .in0(R0_q), .in1(R1_q), .in2(R2_q), .in3(R3_q), .in4(R4_q), .in5(R5_q), .in6(R6_q), .in7(R7_q),
    .in8(R8_q), .in9(R9_q), .in10(R10_q), .in11(R11_q), .in12(R12_q), .in13(R13_q), .in14(R14_q),
    .in15(R15_q), .out(Read_Data_1), .sel(Read_Register_1));  // open: en
  Multiplexer #(.select(4), .width(16)) multiplexer_2 (
    .in0(R0_q), .in1(R1_q), .in2(R2_q), .in3(R3_q), .in4(R4_q), .in5(R5_q), .in6(R6_q), .in7(R7_q),
    .in8(R8_q), .in9(R9_q), .in10(R10_q), .in11(R11_q), .in12(R12_q), .in13(R13_q), .in14(R14_q),
    .in15(R15_q), .out(Read_Data_1_2), .sel(Read_Register_2));  // open: en
endmodule

module alu (
  input  Cin,
  input  A,
  input  B,
  input  [1:0] ALUop,
  input  Binv,
  output out_6,
  output out_7
);

  wire adder_1_out, and_1_out, multiplexer_1_out, not_1_out, or_1_out;

  not not_1 (not_1_out, B);
  Multiplexer multiplexer_1 (.in0(B), .in1(not_1_out), .out(multiplexer_1_out), .sel(Binv));  // open: en
  and and_1 (and_1_out, A, B);
  or or_1 (or_1_out, A, B);
  Adder #(.width(1)) adder_1 (.a(A), .b(multiplexer_1_out), .out(adder_1_out), .cin(Cin), .cout(out_7));
  Multiplexer #(.select(2)) multiplexer_2 (
    .in0(and_1_out), .in1(or_1_out), .in2(adder_1_out), .out(out_6), .sel(ALUop));  // open: in3, en
endmodule

module _16bitalu (
  input  [1:0] ALUop,
  input  Binv,
  input  Cin,
  input  [15:0] A,
  input  [15:0] B,
  output [15:0] S,
  output Zero,
  output Overflow,
  output Cout
);

  wire alu_1_out_7, alu_2_out_7, alu_3_out_7, alu_4_out_7, alu_5_out_7, alu_6_out_7, alu_7_out_7,
       alu_8_out_7, alu_9_out_7, alu_10_out_7, alu_11_out_7, alu_12_out_7, alu_13_out_7, alu_14_out_7,
       alu_15_out_7;

  alu alu_1 (.Cin(Cin), .A(A[0]), .B(B[0]), .out_6(S[0]), .out_7(alu_1_out_7), .ALUop(ALUop), .Binv(Binv));
  alu alu_2 (.Cin(alu_1_out_7), .A(A[1]), .B(B[1]), .out_6(S[1]), .out_7(alu_2_out_7), .ALUop(ALUop), .Binv(Binv));
  alu alu_3 (.Cin(alu_2_out_7), .A(A[2]), .B(B[2]), .out_6(S[2]), .out_7(alu_3_out_7), .ALUop(ALUop), .Binv(Binv));
  alu alu_4 (.Cin(alu_3_out_7), .A(A[3]), .B(B[3]), .out_6(S[3]), .out_7(alu_4_out_7), .ALUop(ALUop), .Binv(Binv));
  alu alu_5 (.Cin(alu_4_out_7), .A(A[4]), .B(B[4]), .out_6(S[4]), .out_7(alu_5_out_7), .ALUop(ALUop), .Binv(Binv));
  alu alu_6 (.Cin(alu_5_out_7), .A(A[5]), .B(B[5]), .out_6(S[5]), .out_7(alu_6_out_7), .ALUop(ALUop), .Binv(Binv));
  alu alu_7 (.Cin(alu_6_out_7), .A(A[6]), .B(B[6]), .out_6(S[6]), .out_7(alu_7_out_7), .ALUop(ALUop), .Binv(Binv));
  alu alu_8 (.Cin(alu_7_out_7), .A(A[7]), .B(B[7]), .out_6(S[7]), .out_7(alu_8_out_7), .ALUop(ALUop), .Binv(Binv));
  alu alu_9 (.Cin(alu_8_out_7), .A(A[8]), .B(B[8]), .out_6(S[8]), .out_7(alu_9_out_7), .ALUop(ALUop), .Binv(Binv));
  alu alu_10 (.Cin(alu_9_out_7), .A(A[9]), .B(B[9]), .out_6(S[9]), .out_7(alu_10_out_7), .ALUop(ALUop), .Binv(Binv));
  alu alu_11 (
    .Cin(alu_10_out_7), .A(A[10]), .B(B[10]), .out_6(S[10]), .out_7(alu_11_out_7), .ALUop(ALUop), .Binv(Binv));
  alu alu_12 (
    .Cin(alu_11_out_7), .A(A[11]), .B(B[11]), .out_6(S[11]), .out_7(alu_12_out_7), .ALUop(ALUop), .Binv(Binv));
  alu alu_13 (
    .Cin(alu_12_out_7), .A(A[12]), .B(B[12]), .out_6(S[12]), .out_7(alu_13_out_7), .ALUop(ALUop), .Binv(Binv));
  alu alu_14 (
    .Cin(alu_13_out_7), .A(A[13]), .B(B[13]), .out_6(S[13]), .out_7(alu_14_out_7), .ALUop(ALUop), .Binv(Binv));
  alu alu_15 (
    .Cin(alu_14_out_7), .A(A[14]), .B(B[14]), .out_6(S[14]), .out_7(alu_15_out_7), .ALUop(ALUop), .Binv(Binv));
  alu alu_16 (.Cin(alu_15_out_7), .A(A[15]), .B(B[15]), .out_6(S[15]), .out_7(Cout), .ALUop(ALUop), .Binv(Binv));
  xor xor_1 (Overflow, alu_15_out_7, Cout);
  nor nor_1 (Zero, S[0], S[1], S[2], S[3], S[4], S[5], S[6], S[7], S[8], S[10], S[11], S[12], S[13], S[14], S[15], S[9]);
endmodule

module reg_alu (
  input  [1:0] ALUop,
  input  B_inv,
  input  Cin,
  input  [3:0] Write_Register,
  input  CLK,
  input  [3:0] Read_Register_1,
  input  Write_Enable,
  input  [3:0] Read_Register_2,
  output Zero,
  output Overflow,
  output Cout
);

  wire [15:0] main_1_read_data_1, main_1_read_data_1_2, n16bitalu_1_s;

  main main_1 (
    .Write_Data(n16bitalu_1_s), .Write_Register(Write_Register), .Read_Data_1(main_1_read_data_1),
    .Read_Data_1_2(main_1_read_data_1_2), .Read_Register_1(Read_Register_1),
    .Read_Register_2(Read_Register_2), .WriteEn(Write_Enable), .CLK(CLK));
  _16bitalu u_16bitalu_1 (
    .S(n16bitalu_1_s), .Zero(Zero), .Overflow(Overflow), .Cout(Cout), .A(main_1_read_data_1),
    .B(main_1_read_data_1_2), .ALUop(ALUop), .Binv(B_inv), .Cin(Cin));
endmodule

module fetch_unit (
  input  in_1,
  input  [1:0] in_2,
  input  in_3,
  input  in_4,
  output out_5,
  output out_6,
  output out_7
);

  wire CLK_out;
  wire [15:0] adder_1_out, main_1_read_data_1, main_1_read_data_1_2, n16bitalu_1_s, Program_Counter_q,
       rom_1_data;

  Adder #(.width(16)) adder_1 (.a(16'h1), .b(Program_Counter_q), .out(adder_1_out));  // open: cin, cout
  Register #(.width(16)) Program_Counter (.D(adder_1_out), .Q(Program_Counter_q), .clk(CLK_out));  // open: en, clr
  Button CLK (.out(CLK_out));
  ROM #(.addrWidth(16), .dataWidth(16)) rom_1 (.addr(Program_Counter_q), .data(rom_1_data));  // open: sel
  main main_1 (
    .Write_Data(n16bitalu_1_s), .Write_Register(rom_1_data[3:0]), .Read_Data_1(main_1_read_data_1),
    .Read_Data_1_2(main_1_read_data_1_2), .Read_Register_1(rom_1_data[11:8]),
    .Read_Register_2(rom_1_data[7:4]), .WriteEn(in_1), .CLK(CLK_out));
  _16bitalu u_16bitalu_1 (
    .S(n16bitalu_1_s), .Zero(out_5), .Overflow(out_6), .Cout(out_7), .A(main_1_read_data_1),
    .B(main_1_read_data_1_2), .ALUop(in_2), .Binv(in_3), .Cin(in_4));
  RAM #(.addrWidth(16), .dataWidth(16)) ram_1 ();  // open: addr, data, sel, clk, ld, clr

  // Notes on the sheet:
  //   R1 + R2
  //   ADD: 3, 0011
  //   0011 0001 0010 0101
  //   Represent in hexa: 3125
  //   Instruction Memory
  //   contents of rom_1 (hex, n*v repeats v):
  //   3125 1111 3125 3125 0 3125
  //   rd
  //   rt
  //   rs
  //   opcode
endmodule

module control_unit (
  input  [3:0] OPcode,
  output Write_Enable,
  output Binv,
  output Cin
);

  wire decoder_1_out0, decoder_1_out1, decoder_1_out2, decoder_1_out4, decoder_1_out5, decoder_1_out6,
       decoder_1_out7, decoder_1_out8, decoder_1_out9, decoder_1_out10, decoder_1_out11, decoder_1_out12,
       decoder_1_out13, decoder_1_out14, decoder_1_out15;

  Decoder #(.select(4)) decoder_1 (
    .out0(decoder_1_out0), .out1(decoder_1_out1), .out2(decoder_1_out2), .out3(Binv), .out4(decoder_1_out4),
    .out5(decoder_1_out5), .out6(decoder_1_out6), .out7(decoder_1_out7), .out8(decoder_1_out8),
    .out9(decoder_1_out9), .out10(decoder_1_out10), .out11(decoder_1_out11), .out12(decoder_1_out12),
    .out13(decoder_1_out13), .out14(decoder_1_out14), .out15(decoder_1_out15), .sel(OPcode));  // open: en
  or or_1 (Write_Enable, decoder_1_out0, decoder_1_out1, decoder_1_out2, Binv, decoder_1_out4, decoder_1_out5, decoder_1_out8, decoder_1_out9);

  assign Cin = Binv;
endmodule
