// Logisim project Chap4_1_BinaryAdderSubtractor.circ as structural Verilog: 1 circuit, main circuit main
module main (
  input  [3:0] B,
  input  [3:0] A,
  input  Mode,
  output Cout,
  output [3:0] S
);

  wire adder_2_cout, adder_3_cout, adder_4_cout, xor_1_out, xor_2_out, xor_3_out, xor_4_out;

  xor xor_1 (xor_1_out, B[3], Mode);
  Adder #(.width(1)) adder_1 (.a(A[3]), .b(xor_1_out), .out(S[3]), .cin(adder_2_cout), .cout(Cout));
  xor xor_2 (xor_2_out, Mode, B[2]);
  Adder #(.width(1)) adder_2 (.a(A[2]), .b(xor_2_out), .out(S[2]), .cin(adder_3_cout), .cout(adder_2_cout));
  xor xor_3 (xor_3_out, Mode, B[1]);
  Adder #(.width(1)) adder_3 (.a(A[1]), .b(xor_3_out), .out(S[1]), .cin(adder_4_cout), .cout(adder_3_cout));
  xor xor_4 (xor_4_out, Mode, B[0]);
  Adder #(.width(1)) adder_4 (.a(A[0]), .b(xor_4_out), .out(S[0]), .cin(Mode), .cout(adder_4_cout));
endmodule
