// Logisim project Chap4_2_BinaryIncrementor.circ as structural Verilog: 1 circuit, main circuit main
module main (
  input  A0,
  input  A3,
  input  A2,
  input  A1,
  output S0,
  output S1,
  output S2,
  output S3,
  output Cout
);

  wire adder_2_cout, adder_3_cout, adder_4_cout;

  Adder #(.width(1)) adder_1 (.a(A3), .b(adder_2_cout), .out(S3), .cout(Cout));  // open: cin
  Adder #(.width(1)) adder_2 (.a(A2), .b(adder_3_cout), .out(S2), .cout(adder_2_cout));  // open: cin
  Adder #(.width(1)) adder_3 (.a(A1), .b(adder_4_cout), .out(S1), .cout(adder_3_cout));  // open: cin
  Adder #(.width(1)) adder_4 (.a(A0), .b(1'b1), .out(S0), .cout(adder_4_cout));  // open: cin
endmodule
